// Logisim project Expo.circ as structural Verilog: 1 circuit, main circuit main
module main (
  input  A,
  input  B,
  output NOT,
  output AND,
  output OR,
  output NAND,
  output NOR,
  output XOR,
  output XNOR
);

  not not_1 (NOT, A);
  and and_1 (AND, A, B);
  or or_1 (OR, A, B);
  nand nand_1 (NAND, A, B);
  nor nor_1 (NOR, A, B);
  xor xor_1 (XOR, A, B);
  xnor xnor_1 (XNOR, A, B);

  // Notes on the sheet:
  //   Basic+universal gates on shared inputs A,B(NOT acts on A only)
endmodule
